// Logisim project control_logic.circ as structural Verilog: 1 circuit, main circuit control_logic
module control_logic (
  input  [31:0] inst,
  input  BrEq,
  input  BrLt,
  output PCSel,
  output RegWEn,
  output [2:0] ImmSel,
  output BrUn,
  output ASel,
  output BSel,
  output [3:0] ALUSel,
  output MemRW,
  output [1:0] WBSel,
  output CSRSel,
  output CSRWen
);

  wire beq_out, bge_out, bgeu_out, blt_out, bltu_out, bne_out, comparator_1_eq, comparator_2_eq,
       comparator_3_eq, comparator_8_eq, comparator_9_eq, comparator_16_eq, comparator_17_eq,
       comparator_18_eq, comparator_19_eq, comparator_20_eq, comparator_21_eq, comparator_22_eq,
       comparator_23_eq, comparator_24_eq, comparator_25_eq, comparator_26_eq, comparator_27_eq,
       comparator_28_eq, comparator_29_eq, is_auipc, is_B_format, is_I_format, is_J_format, is_jalr, is_load,
       is_lui, is_mul, is_mulh, is_R_format, is_sra_or_srai, is_sub, is_U_format, not_1_out, not_2_out,
       not_3_out, or_1_out, or_2_out, or_4_out, or_7_out, or_9_out, or_10_out, or_11_out;
  wire [1:0] multiplexer_4_out;
  wire [2:0] multiplexer_2_out, multiplexer_5_out, multiplexer_8_out, multiplexer_11_out;
  wire [3:0] multiplexer_1_out, multiplexer_3_out, multiplexer_6_out, multiplexer_9_out, multiplexer_10_out,
       multiplexer_12_out;

  Multiplexer #(.enable("false"), .select(3), .width(4)) multiplexer_1 (
    .in0(4'b0000), .in1(4'b0110), .in2(4'b0111), .in3(4'b1011), .in4(4'b0011), .in5(4'b0100), .in6(4'b0010),
    .in7(4'b0001), .out(multiplexer_1_out), .sel(inst[14:12]));
  Multiplexer #(.enable("false"), .width(3)) multiplexer_2 (
    .in0(3'b000), .in1(3'b001), .out(multiplexer_2_out), .sel(MemRW));
  Multiplexer #(.enable("false"), .width(4)) multiplexer_3 (
    .in0(multiplexer_1_out), .in1(4'b1100), .out(multiplexer_3_out), .sel(is_sub));
  Multiplexer #(.enable("false"), .width(2)) multiplexer_4 (
    .in0(2'b00), .in1(2'b01), .out(multiplexer_4_out), .sel(or_1_out));
  or or_1 (or_1_out, is_R_format, is_U_format, is_I_format);
  or or_2 (or_2_out, is_jalr, is_J_format);
  Multiplexer #(.enable("false"), .width(3)) multiplexer_5 (
    .in0(multiplexer_2_out), .in1(3'b010), .out(multiplexer_5_out), .sel(is_B_format));
  or or_3 (RegWEn, is_R_format, is_I_format, is_load, is_jalr, is_J_format, is_U_format);
  Multiplexer #(.enable("false"), .width(4)) multiplexer_6 (
    .in0(multiplexer_3_out), .in1(4'b1010), .out(multiplexer_6_out), .sel(is_mul));
  Multiplexer #(.enable("false"), .width(2)) multiplexer_7 (
    .in0(multiplexer_4_out), .in1(2'b10), .out(WBSel), .sel(or_2_out));
  Multiplexer #(.enable("false"), .width(3)) multiplexer_8 (
    .in0(multiplexer_5_out), .in1(3'b011), .out(multiplexer_8_out), .sel(is_U_format));
  Multiplexer #(.enable("false"), .width(4)) multiplexer_9 (
    .in0(multiplexer_6_out), .in1(4'b1110), .out(multiplexer_9_out), .sel(is_mulh));
  Multiplexer #(.enable("false"), .width(4)) multiplexer_10 (
    .in0(multiplexer_9_out), .in1(4'b0101), .out(multiplexer_10_out), .sel(is_sra_or_srai));
  Multiplexer #(.enable("false"), .width(3)) multiplexer_11 (
    .in0(multiplexer_8_out), .in1(3'b100), .out(multiplexer_11_out), .sel(is_J_format));
  Multiplexer #(.enable("false"), .width(4)) multiplexer_12 (
    .in0(4'b0000), .in1(multiplexer_10_out), .out(multiplexer_12_out), .sel(or_4_out));
  or or_4 (or_4_out, is_R_format, is_I_format);
  Multiplexer #(.enable("false"), .width(3)) multiplexer_13 (
    .in0(multiplexer_11_out), .in1(3'b101), .out(ImmSel), .sel(CSRWen));
  Comparator #(.width(3)) comparator_1 (.a(inst[14:12]), .b(3'b101), .eq(comparator_1_eq));  // open: gt, lt
  Multiplexer #(.enable("false"), .width(4)) multiplexer_14 (
    .in0(multiplexer_12_out), .in1(4'b1101), .out(ALUSel), .sel(is_lui));
  or or_5 (BSel, is_I_format, is_load, is_B_format, is_jalr, is_J_format, is_U_format);
  or or_6 (ASel, is_B_format, is_J_format, is_auipc);
  and and_1 (CSRSel, CSRWen, comparator_1_eq);
  Comparator #(.width(3)) comparator_2 (.a(inst[14:12]), .b(3'b110), .eq(comparator_2_eq));  // open: gt, lt
  Comparator #(.width(3)) comparator_3 (.a(inst[14:12]), .b(3'b111), .eq(comparator_3_eq));  // open: gt, lt
  or or_7 (or_7_out, comparator_2_eq, comparator_3_eq);
  and and_2 (BrUn, or_7_out, is_B_format);
  Comparator #(.width(7)) comparator_4 (.a(inst[6:0]), .b(7'b0110011), .eq(is_R_format));  // open: gt, lt
  Comparator #(.width(7)) comparator_5 (.a(inst[6:0]), .b(7'b0010011), .eq(is_I_format));  // open: gt, lt
  Comparator #(.width(7)) comparator_6 (.a(inst[6:0]), .b(7'b0100011), .eq(MemRW));  // open: gt, lt
  Comparator #(.width(7)) comparator_7 (.a(inst[6:0]), .b(7'b1100011), .eq(is_B_format));  // open: gt, lt
  Comparator #(.width(7)) comparator_8 (.a(inst[6:0]), .b(7'b0010111), .eq(comparator_8_eq));  // open: gt, lt
  Comparator #(.width(7)) comparator_9 (.a(inst[6:0]), .b(7'b0110111), .eq(comparator_9_eq));  // open: gt, lt
  Comparator #(.width(7)) comparator_10 (.a(inst[6:0]), .b(7'b1101111), .eq(is_J_format));  // open: gt, lt
  Comparator #(.width(7)) comparator_11 (.a(inst[6:0]), .b(7'b1110011), .eq(CSRWen));  // open: gt, lt
  Comparator #(.width(7)) comparator_12 (.a(inst[6:0]), .b(7'b0000011), .eq(is_load));  // open: gt, lt
  Comparator #(.width(7)) comparator_13 (.a(inst[6:0]), .b(7'b1100111), .eq(is_jalr));  // open: gt, lt
  Comparator #(.width(7)) comparator_14 (.a(inst[6:0]), .b(7'b0010111), .eq(is_auipc));  // open: gt, lt
  Comparator #(.width(7)) comparator_15 (.a(inst[6:0]), .b(7'b0110111), .eq(is_lui));  // open: gt, lt
  or or_8 (is_U_format, comparator_8_eq, comparator_9_eq);
  Comparator #(.width(3)) comparator_16 (.a(inst[14:12]), .b(3'b000), .eq(comparator_16_eq));  // open: gt, lt
  Comparator #(.width(3)) comparator_17 (.a(inst[14:12]), .b(3'b001), .eq(comparator_17_eq));  // open: gt, lt
  not not_1 (not_1_out, BrEq);
  Comparator #(.width(3)) comparator_18 (.a(inst[14:12]), .b(3'b100), .eq(comparator_18_eq));  // open: gt, lt
  Comparator #(.width(3)) comparator_19 (.a(inst[14:12]), .b(3'b101), .eq(comparator_19_eq));  // open: gt, lt
  not not_2 (not_2_out, BrLt);
  Comparator #(.width(3)) comparator_20 (.a(inst[14:12]), .b(3'b110), .eq(comparator_20_eq));  // open: gt, lt
  Comparator #(.width(3)) comparator_21 (.a(inst[14:12]), .b(3'b111), .eq(comparator_21_eq));  // open: gt, lt
  not not_3 (not_3_out, BrLt);
  and beq (beq_out, comparator_16_eq, is_B_format, BrEq);
  and bne (bne_out, comparator_17_eq, is_B_format, not_1_out);
  and blt (blt_out, comparator_18_eq, is_B_format, BrLt);
  and bge (bge_out, comparator_19_eq, is_B_format, not_2_out);
  and bltu (bltu_out, comparator_20_eq, is_B_format, BrLt);
  and bgeu (bgeu_out, comparator_21_eq, is_B_format, not_3_out);
  Comparator #(.width(3)) comparator_22 (.a(inst[14:12]), .b(3'b000), .eq(comparator_22_eq));  // open: gt, lt
  Comparator #(.width(7)) comparator_23 (.a(inst[31:25]), .b(7'b0100000), .eq(comparator_23_eq));  // open: gt, lt
  Comparator #(.width(3)) comparator_24 (.a(inst[14:12]), .b(3'b000), .eq(comparator_24_eq));  // open: gt, lt
  Comparator #(.width(7)) comparator_25 (.a(inst[31:25]), .b(7'b0000001), .eq(comparator_25_eq));  // open: gt, lt
  Comparator #(.width(3)) comparator_26 (.a(inst[14:12]), .b(3'b001), .eq(comparator_26_eq));  // open: gt, lt
  Comparator #(.width(7)) comparator_27 (.a(inst[31:25]), .b(7'b0000001), .eq(comparator_27_eq));  // open: gt, lt
  Comparator #(.width(3)) comparator_28 (.a(inst[14:12]), .b(3'b101), .eq(comparator_28_eq));  // open: gt, lt
  Comparator #(.width(7)) comparator_29 (.a(inst[31:25]), .b(7'b0100000), .eq(comparator_29_eq));  // open: gt, lt
  or or_9 (or_9_out, is_R_format, is_I_format);
  or or_10 (or_10_out, beq_out, bne_out, blt_out, bge_out, bltu_out, bgeu_out);
  and and_3 (is_sub, comparator_22_eq, comparator_23_eq, is_R_format);
  and and_4 (is_mul, comparator_24_eq, comparator_25_eq, is_R_format);
  and and_5 (is_mulh, comparator_26_eq, comparator_27_eq, is_R_format);
  and and_6 (is_sra_or_srai, comparator_28_eq, comparator_29_eq, or_9_out);
  or or_11 (or_11_out, is_jalr, is_J_format);
  or or_12 (PCSel, or_10_out, or_11_out);

  // Other names for the same wires on the sheet: opcode[6:0] = inst[6:0]; rd[4:0] = inst[11:7];
  //   funct3[2:0] = inst[14:12]; rs1[4:0] = inst[19:15]; rs2[4:0] = inst[24:20]; funct7[6:0] = inst[31:25];
  //   is_CSR_format = CSRWen; is_S_format = MemRW

  // Notes on the sheet:
  //   INPUTS to your circuit
  //   RegWEn
  //   WBSel
  //   ImmSel
  //   ALUSel
  //   DON'T CHANGE THE LOCATIONS OF THE INPUTS AND OUTPUTS!
  //   OUTPUT from your circuit
  //   BSel and ASel
  //   CSRSel and CSRWen
  //   BrUn
  //   is what
  //   PCSel
endmodule
