// Logisim project cpu.circ as structural Verilog: 1 circuit, main circuit cpu
module cpu (
  input  clk,
  input  [31:0] INSTRUCTION,
  input  [31:0] READ_DATA,
  output [31:0] WRITE_ADDRESS,
  output [31:0] PROGRAM_COUNTER,
  output [31:0] ra,
  output [31:0] sp,
  output [31:0] t0,
  output [31:0] t1,
  output [31:0] t2,
  output [31:0] s0,
  output [31:0] s1,
  output [31:0] a0,
  output [31:0] tohost,
  output [3:0] WRITE_ENABLE,
  output [31:0] WRITE_DATA
);

  wire and_1_out, and_2_out, ASel, BrEq, BrLt, BrUn, BSel, comparator_1_eq, comparator_2_eq, comparator_3_eq,
       comparator_4_eq, comparator_5_eq, comparator_6_eq, comparator_7_eq, comparator_8_eq, CSRSEL, CSRWen,
       is_sb_out, is_sh_out, MemRW, PCSel, RegWEn;
  wire [1:0] WBSel;
  wire [2:0] funct3, ImmSel;
  wire [3:0] ALUSel, multiplexer_9_out, multiplexer_10_out;
  wire [6:0] funct7;
  wire [24:0] INSTRUCTION_NEW;
  wire [31:0] adder_1_out, CSRdin, imm, multiplexer_1_out, multiplexer_2_out, multiplexer_3_out,
       multiplexer_4_out, multiplexer_6_out, PCAdd4, PROGRAM_COUNTER_NEW, READ_DATA_1byte, READ_DATA_final,
       READ_DATA_halfword, readData1, writeData;

  Adder #(.width(32)) adder_1 (.a(PROGRAM_COUNTER), .b(32'h4), .out(adder_1_out));  // open: cin, cout
  Multiplexer #(.enable("false"), .width(32)) multiplexer_1 (
    .in0(adder_1_out), .in1(WRITE_ADDRESS), .out(multiplexer_1_out), .sel(PCSel));
  Register #(.width(32)) PC (.D(multiplexer_1_out), .clk(clk), .Q(PROGRAM_COUNTER));  // open: en, clr
  Multiplexer #(.enable("false"), .width(32)) multiplexer_2 (
    .in0(INSTRUCTION), .in1(32'h13), .out(multiplexer_2_out), .sel(PCSel));
  Register #(.width(32)) register_1 (.D(PROGRAM_COUNTER), .clk(clk), .Q(PROGRAM_COUNTER_NEW));  // open: en, clr
  Register #(.width(32)) register_2 (
    .D(multiplexer_2_out), .clk(clk), .Q({funct7, INSTRUCTION_NEW[24:15], funct3, INSTRUCTION_NEW[11:0]}));  // open: en, clr
  control_logic control_logic_1 (
    .CSRWen(CSRWen), .PCSel(PCSel), .RegWEn(RegWEn), .ImmSel(ImmSel), .BrUn(BrUn), .ASel(ASel), .BSel(BSel),
    .ALUSel(ALUSel), .MemRW(MemRW), .WBSel(WBSel), .CSRSel(CSRSEL),
    .inst({funct7, INSTRUCTION_NEW[24:15], funct3, INSTRUCTION_NEW[11:0]}), .BrEq(BrEq), .BrLt(BrLt));
  regfile regfile_1 (
    .rs1(INSTRUCTION_NEW[19:15]), .rs2(INSTRUCTION_NEW[24:20]), .rd(INSTRUCTION_NEW[11:7]),
    .Write_Data(writeData), .RegWEn(RegWEn), .clk(clk), .ra(ra), .sp(sp), .t0(t0), .t1(t1), .t2(t2), .s0(s0),
    .s1(s1), .a0(a0), .Read_Data_1(readData1), .Read_Data_2(WRITE_DATA));
  branch_comp branch_comp_1 (.rs1(readData1), .rs2(WRITE_DATA), .BrUn(BrUn), .BrEq(BrEq), .BrLt(BrLt));
  imm_gen imm_gen_1 (
    .inst({funct7, INSTRUCTION_NEW[24:15], funct3, INSTRUCTION_NEW[11:0]}), .ImmSel(ImmSel), .imm(imm));
  Multiplexer #(.enable("false"), .width(32)) multiplexer_3 (
    .in0(readData1), .in1(PROGRAM_COUNTER_NEW), .out(multiplexer_3_out), .sel(ASel));
  Multiplexer #(.enable("false"), .width(32)) multiplexer_4 (
    .in0(WRITE_DATA), .in1(imm), .out(multiplexer_4_out), .sel(BSel));
  Multiplexer #(.enable("false"), .width(32)) multiplexer_5 (.in0(readData1), .in1(imm), .out(CSRdin), .sel(CSRSEL));
  csr csr_1 (.CSR_address(12'h51e), .CSR_din(CSRdin), .CSR_WE(CSRWen), .clk(clk), .tohost(tohost));
  alu alu_1 (.Result(WRITE_ADDRESS), .A(multiplexer_3_out), .B(multiplexer_4_out), .ALUSel(ALUSel));
  Comparator #(.width(3)) comparator_1 (.a(funct3), .b(3'b000), .eq(comparator_1_eq));  // open: gt, lt
  Comparator #(.width(7)) comparator_2 (
    .a(INSTRUCTION_NEW[6:0]), .b(7'b0000011), .eq(comparator_2_eq));  // open: gt, lt
  Multiplexer #(.enable("false"), .width(32)) multiplexer_6 (
    .in0(READ_DATA), .in1(READ_DATA_1byte), .out(multiplexer_6_out), .sel(and_1_out));
  and and_1 (and_1_out, comparator_1_eq, comparator_2_eq);
  assign READ_DATA_1byte = {{24{READ_DATA[7]}}, READ_DATA[7:0]};  // Bit_Extender bit_extender_1
  assign READ_DATA_halfword = {{16{READ_DATA[15]}}, READ_DATA[15:0]};  // Bit_Extender bit_extender_2
  Comparator #(.width(3)) comparator_3 (.a(funct3), .b(3'b001), .eq(comparator_3_eq));  // open: gt, lt
  Comparator #(.width(7)) comparator_4 (
    .a(INSTRUCTION_NEW[6:0]), .b(7'b0100011), .eq(comparator_4_eq));  // open: gt, lt
  Multiplexer #(.enable("false"), .width(32)) multiplexer_7 (
    .in0(multiplexer_6_out), .in1(READ_DATA_halfword), .out(READ_DATA_final), .sel(and_2_out));
  and and_2 (and_2_out, comparator_5_eq, comparator_6_eq);
  Comparator #(.width(3)) comparator_5 (.a(funct3), .b(3'b001), .eq(comparator_5_eq));  // open: gt, lt
  Comparator #(.width(7)) comparator_6 (
    .a(INSTRUCTION_NEW[6:0]), .b(7'b0000011), .eq(comparator_6_eq));  // open: gt, lt
  Multiplexer #(.enable("false"), .select(2), .width(32)) multiplexer_8 (
    .in0(READ_DATA_final), .in1(WRITE_ADDRESS), .in2(PCAdd4), .out(writeData), .sel(WBSel));  // open: in3
  Adder #(.width(32)) adder_2 (.a(PROGRAM_COUNTER_NEW), .b(32'h4), .out(PCAdd4));  // open: cin, cout
  Multiplexer #(.enable("false"), .width(4)) multiplexer_9 (
    .in0(4'b1111), .in1(4'b0011), .out(multiplexer_9_out), .sel(is_sh_out));
  and is_sh (is_sh_out, comparator_3_eq, comparator_4_eq);
  Multiplexer #(.enable("false"), .width(4)) multiplexer_10 (
    .in0(multiplexer_9_out), .in1(4'b0001), .out(multiplexer_10_out), .sel(is_sb_out));
  and is_sb (is_sb_out, comparator_7_eq, comparator_8_eq);
  Comparator #(.width(3)) comparator_7 (.a(funct3), .b(3'b000), .eq(comparator_7_eq));  // open: gt, lt
  Comparator #(.width(7)) comparator_8 (
    .a(INSTRUCTION_NEW[6:0]), .b(7'b0100011), .eq(comparator_8_eq));  // open: gt, lt
  Multiplexer #(.enable("false"), .width(4)) multiplexer_11 (
    .in0(4'b0000), .in1(multiplexer_10_out), .out(WRITE_ENABLE), .sel(MemRW));

  // Other names for the same wires on the sheet: READ_DATA_1word[31:0] = READ_DATA; ALUOUT[31:0] = WRITE_ADDRESS;
  //   opcode[6:0] = INSTRUCTION_NEW[6:0]; rd[4:0] = INSTRUCTION_NEW[11:7];
  //   INSTRUCTION_NEW (some bits) = {funct7, funct3}; rs1[4:0] = INSTRUCTION_NEW[19:15];
  //   rs2[4:0] = INSTRUCTION_NEW[24:20]; readData2[31:0] = WRITE_DATA

  // Notes on the sheet:
  //   NOP:addi x0, x0, 0
  //   Output to IMEM
  //   IMEM (do **NOT** move this)
  //   Inputs from IMEM
  //   It is OK to move the PC, RegFile, ALU, MEM, Branch Comp, Imm Gen, and Control Logic to wherever is most convenient for you when constructing your CPU, and to delete this text
  //   Inputs/Outputs for testing. Do **NOT** move these.
  //   deal with lw lb lh
  //   Outputs To DMEM
  //   DMEM (do **NOT** move this)
  //   Inputs From DMEM
  //   deal with sw sb sh
  //   0xf:0b1111->sw, 0x3:0b0011->sh, 0x1:0b0001->sb, 0x0:0b0000->no write
endmodule
